// Logisim project floor_traversal.circ as structural Verilog: 1 circuit, main circuit main
module main (
  input  [1:0] in_1,
  input  in_2,
  input  in_3,
  output [1:0] out_4
);

  wire and_1_out, and_2_out, and_3_out, not_1_out, not_2_out, not_3_out, not_4_out, or_1_out, or_2_out,
       xor_1_out;

  not not_1 (not_1_out, in_2);
  xor xor_1 (xor_1_out, in_1[1], out_4[1]);
  not not_2 (not_2_out, in_1[0]);
  and and_1 (and_1_out, not_1_out, in_3);
  not not_3 (not_3_out, out_4[0]);
  not not_4 (not_4_out, in_1[1]);
  or or_1 (or_1_out, in_1[0], xor_1_out);
  or or_2 (or_2_out, not_2_out, xor_1_out);
  and and_2 (and_2_out, out_4[0], in_1[1]);
  and and_3 (and_3_out, not_3_out, not_4_out);
  J_K_Flip_Flop j_k_ff_1 (.J(and_2_out), .clk(and_1_out), .K(and_3_out), .Q(out_4[1]));  // open: Qn, preset, en, reset
  J_K_Flip_Flop j_k_ff_2 (.J(or_1_out), .clk(and_1_out), .K(or_2_out), .Q(out_4[0]));  // open: Qn, preset, en, reset

  // Notes on the sheet:
  //   Working Circuit
endmodule
