// Logisim project main_file.circ as structural Verilog: 1 circuit, main circuit main
module main (
  input  in_1,
  input  in_2,
  input  in_3,
  input  in_4,
  input  in_5,
  output out_6,
  output out_7,
  output out_8
);

  wire clock_1_out, main_2_out_5, main_2_out_6, main_2_out_7, main_2_out_8, main_2_out_9, main_2_out_10,
       main_2_out_11;
  wire [1:0] main_1_out_4, priority_encoder_1_out;

  Priority_Encoder #(.select(2)) priority_encoder_1 (
    .in0(in_1), .in1(in_2), .in2(in_3), .in3(in_5), .out(priority_encoder_1_out));  // open: gs, en_out, en_in
  Clock clock_1 (.out(clock_1_out));
  floor_traversal_main main_1 (.in_1(priority_encoder_1_out), .in_2(in_4), .in_3(clock_1_out), .out_4(main_1_out_4));
  _7_SEGMENT_PRACTICAL3_main main_2 (
    .out_5(main_2_out_5), .out_6(main_2_out_6), .out_7(main_2_out_7), .out_8(main_2_out_8),
    .out_10(main_2_out_10), .out_11(main_2_out_11), .X(1'b0), .W(1'b0), .Z(main_1_out_4[0]),
    .Y(main_1_out_4[1]), .out_9(main_2_out_9));
  Comparator #(.width(2)) comparator_1 (
    .a(main_1_out_4), .b(priority_encoder_1_out), .gt(out_6), .eq(out_7), .lt(out_8));
  _7_Segment_Display u_7_segment_display_1 (
    .g(main_2_out_11), .f(main_2_out_5), .a(main_2_out_6), .b(main_2_out_7), .e(main_2_out_10),
    .d(main_2_out_9), .c(main_2_out_8));  // open: dp
endmodule
